# Fritzing sketch DistanceBeep (saved by Fritzing 0.9.3b)
breadboards: 1

parts:
  Onderdeel1 = Arduino Uno (Rev3) - ICSP
  hc-sr1 = hc-sr04
  J1 = Piezo Speaker

nets:
  N1: Onderdeel1.D9_PWM, hc-sr1.Trig
  N2: Onderdeel1.D10_PWM/SS, hc-sr1.Echo
  N3: Onderdeel1.D11_PWM/MOSI, J1.pin2
  5V: Onderdeel1.5V, hc-sr1.VCC, J1.pin1
  GND: Onderdeel1.GND, hc-sr1.GND
